# Fritzing sketch james (saved by Fritzing 0.9.3b)
breadboards: 1

parts:
  IC1 = L293D [package=THT]
  M1 = DC Motor
  Part1 = Arduino Uno (Rev3)
  VCC1 = 4 x AAA Battery Mount
  M2 = DC Motor
  U1 = ESP8266 WiFi Module [part_number=ESP8266]

nets:
  N1: IC1.Enable_1, IC1.+Vmotor, IC1.Enable_2, IC1.+V, Part1.VIN, VCC1.+
  N2: IC1.In_1, Part1.D5_PWM
  N3: IC1.Out_1_(_Controlled_by_Enable_1_), M2.pin_2
  GND: IC1.0V, Part1.GND, VCC1.-, U1.GND
  N4: IC1.Out_2_(_Controlled_by_Enable_1_), M2.pin_1
  N5: IC1.In_2, Part1.D4
  N6: IC1.In_3, Part1.D7
  N7: IC1.Out_3_(_Controlled_by_Enable_2_), M1.pin_2
  N8: IC1.Out_4_(_Controlled_by_Enable_2_), M1.pin_1
  N9: IC1.In_4, Part1.D6_PWM
  N10: Part1.D0/RX, U1.TXD
  N11: Part1.D1/TX, U1.RXD
  N12: Part1.D2, U1.GPIO_0
  3V3: Part1.3V3, U1.VCC, U1.RST, U1.GPIO_2, U1.CH_PD

custom parts:
  ESP8266 WiFi Module: Generic WiFi Module based on the ESP8266 with onboard PCB antenna and UART communications
